# Fritzing sketch 2 potentiometers (saved by Fritzing 0.8.0b)
breadboards: 1

parts:
  Composants1 = Arduino Uno (Rev3)
  U1 = POT [package=pot_alpha_rv16af-20]
  U2 = POT [package=pot_mammoth]
  R2 = Resistor [tolerance=±5% resistance=220 package=THT]
  R3 = Resistor [tolerance=±5% resistance=220 package=THT]
  U3 = RELAY [package=relay-g5q]  # not connected
  U4 = RELAY-2 [package=relay-g5v]  # not connected

nets:
  N1: Composants1.A0, R3.Pin_0
  N2: Composants1.A1, R2.Pin_0
  N3: Composants1.5V, U1.E, U2.E
  N4: Composants1.GND, U2.S
  N5: U1.S, R3.Pin_1
  N6: U2.A, R2.Pin_1
